# Fritzing sketch LED Matrix Crosshair (saved by Fritzing 0.9.3b)
breadboards: 1

parts:
  Disp1 = LBT2088AH [part_number=LBT2088AH]
  U1 = MAX7219 [package=dil24]
  R1 = Resistor [tolerance=±5% resistance=10k package=THT]
  R2 = Resistor [tolerance=±5% resistance=10k package=THT]
  R3 = Resistor [tolerance=±5% resistance=10k package=THT]
  Part1 = Arduino Uno (Rev3)
  Column_Control = POT [package=pot_mammoth]
  Row_control = POT [package=pot_mammoth]

nets:
  N1: Disp1.pin1, U1.DIG4
  N2: Disp1.pin2, U1.DIG6
  N3: Disp1.pin_3, U1.SEGA
  N4: Disp1.pin_4, U1.SEGB
  N5: Disp1.pin_5, U1.DIG7
  N6: Disp1.pin_6, U1.SEGD
  N7: Disp1.pin_7, U1.DIG5
  N8: Disp1.pin_8, U1.DIG2
  N9: Disp1.pin_9, U1.DIG0
  N10: Disp1.pin_10, U1.SEGC
  N11: Disp1.pin_11, U1.SEGE
  N12: Disp1.pin_12, U1.DIG3
  N13: Disp1.pin_13, U1.SEGDP
  N14: Disp1.pin_14, U1.DIG1
  N15: Disp1.pin_15, U1.SEGF
  N16: Disp1.pin_16, U1.SEGG
  N17: U1.DIN, Part1.D11_PWM/MOSI
  GND: U1.GND, U1.GND2, Part1.GND, Column_Control.S, Row_control.S
  N18: U1.LOAD, Part1.D8
  N19: U1.CLK, Part1.D13/SCK
  N20: U1.ISET, R1.Pin_0
  VCC: U1.VCC, R3.Pin_1, Part1.5V, Column_Control.E, Row_control.E
  N21: R1.Pin_1, R2.Pin_0
  N22: R2.Pin_1, R3.Pin_0
  N23: Part1.A0, Column_Control.A
  N24: Part1.A2, Row_control.A
